# Fritzing sketch pc-autolocker-hid-kb (saved by Fritzing 0.9.5d)
circuit board: 4.15417cm x 3.84433cm

parts:
  Mod1 = Digispark
  Part1 = SRF05 Ultrasonic Rangefinder
  LED1 = LED - 5mm [color="Red (633nm)" package="5 mm [THT]"]
  R1 = Resistor [tolerance=±5% resistance=220 package=THT]
  R2 = Resistor [tolerance=±5% resistance=220 package=THT]
  buz1 = Piezo Buzzer
  Part2 = SRF05 Ultrasonic Rangefinder
  buz2 = Piezo Buzzer
  LED2 = LED - 5mm [color="Red (633nm)" package="5 mm [THT]"]
  R3 = Resistor [tolerance=±5% resistance=220 package=THT]
  R4 = Resistor [tolerance=±5% resistance=220 package=THT]
  A1 = ATTINY85 USB

nets (from the breadboard view):
  VCC: Mod1.VCC, Part1.VCC
  GND: Mod1.GND, Part1.GND, LED1.cathode, buz1.pin_2
  N1: Mod1.P0, Part1.Trig, R1.Pin_1
  N2: Mod1.P1, R2.Pin_0
  N3: Mod1.P2, Part1.Echo
  N4: LED1.anode, R1.Pin_0
  N5: R2.Pin_1, buz1.pin_1
  N6: Part2.VCC, A1.Pin_7
  N7: Part2.Trig, A1.Pin_1
  N8: Part2.Echo, A1.Pin_3
  N9: Part2.GND, buz2.pin_2, LED2.cathode, A1.Pin_8
  N10: buz2.pin_1, R3.Pin_1
  N11: LED2.anode, R4.Pin_0
  N12: R3.Pin_0, A1.Pin_2

custom parts:
  Digispark: The Digispark is an Attiny85 based microcontroller development board similar to the Arduino line, only cheaper, smaller, and a bit less powerful. With a whole host of shields to extend its functionality and the ability to use the familiar Arduino IDE the Digispark is a great way to jump into electronics, or perfect for when an Arduino is too big or too much. May 2019 modified to correct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
  Piezo Buzzer: Part from https://www.nutsvolts.com/magazine/article/november2012_SmileysWorkshop modified to be .3 in spacing to match the adafruit buzzer 5V breadboard friendly part.
  ATTINY85 USB: 6 digital I/O, 3 support PWM and 4 support analog inputs..
